// Logisim project DinoGame.circ as structural Verilog: 3 circuits, main circuit main
module main (
  input  START
);

  wire counter_1_carry, counter_2_carry, d_ff_1_q, demultiplexer_1_out0, demultiplexer_1_out1, JUMP_out,
       Levels_out_4, RESET_out, Ring_Counter_out_1, Ring_Counter_out_2, Ring_Counter_out_3,
       Ring_Counter_out_4, Ring_Counter_out_5;
  wire [1:0] counter_1_q;
  wire [3:0] bit_extender_1_out, counter_2_q;

  Levels Levels (.START(START), .FLAG(demultiplexer_1_out0), .MODE(counter_1_q), .out_4(Levels_out_4));
  Ring_Counter Ring_Counter (
    .CLOCK(Levels_out_4), .RESET(RESET_out), .OUT_1(Ring_Counter_out_1), .OUT_2(Ring_Counter_out_2),
    .OUT_3(Ring_Counter_out_3), .OUT_4(Ring_Counter_out_4), .OUT_5(Ring_Counter_out_5));
  Button RESET (.out(RESET_out));
  LED led_1 (.in(Ring_Counter_out_1));
  LED led_2 (.in(Ring_Counter_out_3));
  LED led_3 (.in(Ring_Counter_out_2));
  LED led_4 (.in(Ring_Counter_out_5));
  LED led_5 (.in(Ring_Counter_out_4));
  Button JUMP (.out(JUMP_out));
  Demultiplexer #(.disabled(0)) demultiplexer_1 (
    .out0(demultiplexer_1_out0), .out1(demultiplexer_1_out1), .in(1'b1), .sel(JUMP_out),
    .en(Ring_Counter_out_5));
  D_Flip_Flop d_ff_1 (
    .clk(demultiplexer_1_out1), .D(counter_2_carry), .Q(d_ff_1_q), .en(1'b1));  // open: Qn, preset, reset
  Counter #(.width(2), .max('h3)) counter_1 (
    .Q(counter_1_q), .carry(counter_1_carry), .clk(d_ff_1_q), .clr(RESET_out));  // open: load, D, count
  LED COMPLETED (.in(counter_1_carry));
  Counter #(.width(4), .max('h9)) counter_2 (
    .Q(counter_2_q), .carry(counter_2_carry), .clk(demultiplexer_1_out1), .clr(RESET_out));  // open: load, D, count
  assign bit_extender_1_out = {{2{1'b0}}, counter_1_q};  // Bit_Extender bit_extender_1
  Hex_Digit_Display hex_digit_display_1 (.value(bit_extender_1_out));  // open: dp
  Hex_Digit_Display hex_digit_display_2 (.value(counter_2_q));  // open: dp

  // Notes on the sheet:
  //   Time that
  //   JUMP!!!!
endmodule

module Ring_Counter (
  input  CLOCK,
  input  RESET,
  output OUT_1,
  output OUT_2,
  output OUT_3,
  output OUT_4,
  output OUT_5
);

  D_Flip_Flop d_ff_1 (.clk(CLOCK), .D(OUT_5), .Q(OUT_1), .preset(RESET), .en(1'b1));  // open: Qn, reset
  D_Flip_Flop d_ff_2 (.clk(CLOCK), .D(OUT_1), .Q(OUT_2), .en(1'b1), .reset(RESET));  // open: Qn, preset
  D_Flip_Flop d_ff_3 (.clk(CLOCK), .D(OUT_2), .Q(OUT_3), .en(1'b1), .reset(RESET));  // open: Qn, preset
  D_Flip_Flop d_ff_4 (.clk(CLOCK), .D(OUT_3), .Q(OUT_4), .en(1'b1), .reset(RESET));  // open: Qn, preset
  D_Flip_Flop d_ff_5 (.clk(CLOCK), .D(OUT_4), .Q(OUT_5), .en(1'b1), .reset(RESET));  // open: Qn, preset
endmodule

module Levels (
  input  START,
  input  FLAG,
  input  [1:0] MODE,
  output out_4
);

  wire and_1_out, clock_1_out, clock_2_out, d_ff_1_q, d_ff_2_q, d_ff_2_qn, multiplexer_1_out, nor_1_out,
       nor_2_out, nor_3_out, nor_4_out, not_1_out, t_ff_1_q, t_ff_1_qn, t_ff_2_q;

  Clock clock_1 (.out(clock_1_out));
  nor nor_1 (nor_1_out, d_ff_1_q, d_ff_2_q);
  D_Flip_Flop d_ff_1 (.clk(clock_1_out), .D(nor_1_out), .Q(d_ff_1_q), .en(1'b1));  // open: Qn, preset, reset
  D_Flip_Flop d_ff_2 (.clk(clock_1_out), .D(d_ff_1_q), .Q(d_ff_2_q), .Qn(d_ff_2_qn), .en(1'b1));  // open: preset, reset
  Clock clock_2 (.out(clock_2_out));
  nor nor_2 (nor_2_out, clock_1_out, clock_1_out);
  T_Flip_Flop t_ff_1 (
    .clk(clock_2_out), .T(clock_2_out), .Q(t_ff_1_q), .Qn(t_ff_1_qn), .en(1'b1));  // open: preset, reset
  nor nor_3 (nor_3_out, nor_2_out, d_ff_2_qn);
  nor nor_4 (nor_4_out, d_ff_1_q, nor_3_out);
  T_Flip_Flop t_ff_2 (.clk(t_ff_1_qn), .T(t_ff_1_qn), .Q(t_ff_2_q), .en(1'b1));  // open: Qn, preset, reset
  Multiplexer #(.select(2), .disabled(0)) multiplexer_1 (
    .in0(t_ff_2_q), .in1(nor_4_out), .in2(t_ff_1_q), .in3(1'b0), .out(multiplexer_1_out), .sel(MODE),
    .en(1'b1));
  and and_1 (and_1_out, multiplexer_1_out, START);
  not not_1 (not_1_out, FLAG);
  and and_2 (out_4, and_1_out, not_1_out);
endmodule
